// Logisim project MUX.circ as structural Verilog: 1 circuit, main circuit main
module main (
  input  in_1,
  output out_2,
  output out_3,
  output out_4
);

  wire clock_1_out, multiplexer_1_out, multiplexer_2_out, multiplexer_3_out, multiplexer_4_out,
       multiplexer_5_out, multiplexer_6_out, multiplexer_7_out, multiplexer_8_out, multiplexer_9_out,
       multiplexer_10_out, not_1_out;
  wire [0:0] d_ff_1_q;

  Multiplexer #(.select(3)) multiplexer_1 (
    .in0(1'b0), .in1(1'b0), .in2(1'b0), .in3(1'b1), .in4(1'b1), .in5(1'b1), .in6(1'b1), .in7(1'b0),
    .out(multiplexer_1_out), .sel({out_4, out_3, d_ff_1_q[0]}));  // open: en
  Multiplexer #(.select(3)) multiplexer_2 (
    .in0(1'b0), .in1(1'b1), .in2(1'b1), .in3(1'b0), .in4(1'b0), .in5(1'b1), .in6(1'b1), .in7(1'b0),
    .out(multiplexer_2_out), .sel({out_4, out_3, d_ff_1_q[0]}));  // open: en
  Multiplexer #(.select(3)) multiplexer_3 (
    .in0(1'b1), .in1(1'b0), .in2(1'b1), .in3(1'b0), .in4(1'b1), .in5(1'b0), .in6(1'b1), .in7(1'b0),
    .out(multiplexer_3_out), .sel({out_4, out_3, d_ff_1_q[0]}));  // open: en
  Clock clock_1 (.out(clock_1_out));
  D_Flip_Flop d_ff_1 (.clk(clock_1_out), .D(multiplexer_1_out), .Q(d_ff_1_q[0]));  // open: Qn, preset, en, reset
  D_Flip_Flop d_ff_2 (.clk(clock_1_out), .D(multiplexer_2_out), .Q(out_3));  // open: Qn, preset, en, reset
  D_Flip_Flop d_ff_3 (.clk(clock_1_out), .D(multiplexer_3_out), .Q(out_4));  // open: Qn, preset, en, reset
  not not_1 (not_1_out, out_4);
  Multiplexer #(.select(3)) multiplexer_4 (
    .in0(1'b1), .in1(1'b1), .in2(not_1_out), .in3(1'b0), .in4(1'b0), .in5(1'b0), .in6(1'b0), .in7(1'b0),
    .out(multiplexer_4_out), .sel({in_1, out_3, d_ff_1_q[0]}));  // open: en
  Multiplexer #(.select(3)) multiplexer_5 (
    .in0(1'b0), .in1(out_4), .in2(1'b1), .in3(out_4), .in4(1'b0), .in5(1'b0), .in6(1'b0), .in7(1'b0),
    .out(multiplexer_5_out), .sel({in_1, out_3, d_ff_1_q[0]}));  // open: en
  Multiplexer #(.select(3)) multiplexer_6 (
    .in0(out_4), .in1(1'b0), .in2(1'b1), .in3(out_4), .in4(1'b0), .in5(1'b0), .in6(1'b0), .in7(1'b0),
    .out(multiplexer_6_out), .sel({in_1, out_3, d_ff_1_q[0]}));  // open: en
  Multiplexer #(.select(3)) multiplexer_7 (
    .in0(1'b1), .in1(1'b1), .in2(not_1_out), .in3(1'b0), .in4(1'b0), .in5(1'b0), .in6(1'b0), .in7(1'b0),
    .out(multiplexer_7_out), .sel({in_1, out_3, d_ff_1_q[0]}));  // open: en
  Multiplexer #(.select(3)) multiplexer_8 (
    .in0(not_1_out), .in1(1'b1), .in2(1'b0), .in3(1'b0), .in4(1'b0), .in5(1'b0), .in6(1'b0), .in7(1'b0),
    .out(multiplexer_8_out), .sel({in_1, out_3, d_ff_1_q[0]}));  // open: en
  Multiplexer #(.select(3)) multiplexer_9 (
    .in0(1'b1), .in1(not_1_out), .in2(1'b0), .in3(1'b0), .in4(1'b0), .in5(1'b0), .in6(1'b0), .in7(1'b0),
    .out(multiplexer_9_out), .sel({in_1, out_3, d_ff_1_q[0]}));  // open: en
  Multiplexer #(.select(3)) multiplexer_10 (
    .in0(out_4), .in1(1'b1), .in2(not_1_out), .in3(not_1_out), .in4(1'b0), .in5(1'b0), .in6(1'b0),
    .in7(1'b0), .out(multiplexer_10_out), .sel({in_1, out_3, d_ff_1_q[0]}));  // open: en
  _7_Segment_Display u_7_segment_display_1 (
    .g(multiplexer_10_out), .f(multiplexer_9_out), .a(multiplexer_4_out), .b(multiplexer_5_out),
    .e(multiplexer_8_out), .d(multiplexer_7_out), .c(multiplexer_6_out));  // open: dp
endmodule
