// Logisim project Sq-counter.circ as structural Verilog: 1 circuit, main circuit main
module main (
);

  wire and_1_out, and_2_out, and_3_out, and_4_out, and_5_out, and_6_out, B_q, B_qn, C_q, C_qn, clock_1_out,
       D_q, D_qn, or_1_out, or_2_out, or_3_out;

  Clock clock_1 (.out(clock_1_out));
  and and_1 (and_1_out, B_q, C_qn);
  and and_2 (and_2_out, B_q, D_qn);
  and and_3 (and_3_out, C_q, D_q);
  and and_4 (and_4_out, and_3_out, B_qn);
  or or_1 (or_1_out, and_1_out, and_2_out);
  or or_2 (or_2_out, or_1_out, and_4_out);
  and and_5 (and_5_out, C_qn, D_q);
  or or_3 (or_3_out, and_5_out, and_6_out);
  and and_6 (and_6_out, C_q, D_qn);
  D_Flip_Flop B (.clk(clock_1_out), .D(or_2_out), .Q(B_q), .Qn(B_qn));  // open: preset, en, reset
  D_Flip_Flop C (.clk(clock_1_out), .D(or_3_out), .Q(C_q), .Qn(C_qn));  // open: preset, en, reset
  D_Flip_Flop D (.clk(clock_1_out), .D(D_qn), .Q(D_q), .Qn(D_qn));  // open: preset, en, reset
  LED led_1 (.in(B_q));
  LED led_2 (.in(C_q));
  LED led_3 (.in(D_q));
endmodule
