// Logisim project Universal Gate Logicim.circ as structural Verilog: 1 circuit, main circuit main
module main (
  input  A,
  input  B,
  input  C
);

  wire and_1_out, and_2_out, and_3_out, and_4_out, and_5_out, and_6_out, and_7_out, and_8_out, and_9_out,
       and_10_out, not_1_out, not_2_out, not_3_out, or_1_out, or_2_out, or_3_out, or_4_out, or_5_out,
       or_6_out, or_7_out, or_8_out, or_9_out;

  not not_1 (not_1_out, A);
  not not_2 (not_2_out, B);
  not not_3 (not_3_out, C);
  and and_1 (and_1_out, not_2_out, not_3_out);
  and and_2 (and_2_out, A, not_2_out);
  and and_3 (and_3_out, B, C);
  or or_1 (or_1_out, A, C);
  and and_4 (and_4_out, not_2_out, not_3_out);
  or or_2 (or_2_out, B, not_3_out);
  or or_3 (or_3_out, not_2_out, not_3_out);
  and and_5 (and_5_out, A, not_3_out);
  or or_4 (or_4_out, B, C);
  and and_6 (and_6_out, or_1_out, not_2_out);
  and and_7 (and_7_out, A, C);
  and and_8 (and_8_out, or_2_out, not_1_out);
  and and_9 (and_9_out, or_3_out, not_1_out);
  and and_10 (and_10_out, or_4_out, not_1_out);
  or or_5 (or_5_out, and_1_out, not_1_out);
  or or_6 (or_6_out, and_2_out, and_3_out);
  or or_7 (or_7_out, and_6_out, and_7_out);
  or or_8 (or_8_out, and_4_out, not_1_out);
  or or_9 (or_9_out, and_5_out, and_10_out);
  _7_Segment_Display u_7_segment_display_1 (
    .g(or_9_out), .f(and_9_out), .a(or_5_out), .b(or_6_out), .e(and_8_out), .d(or_8_out), .c(or_7_out));  // open: dp
endmodule
