// Logisim project project.circ as structural Verilog: 1 circuit, main circuit main
module main (
  input  [2:0] ABC,
  input  in_2,
  input  in_3,
  input  D
);

  wire multiplexer_1_out, multiplexer_2_out, multiplexer_3_out, multiplexer_4_out, multiplexer_5_out,
       multiplexer_6_out, multiplexer_7_out, not_1_out;

  not not_1 (not_1_out, D);
  Multiplexer #(.select(3)) multiplexer_1 (
    .in0(in_3), .in1(in_3), .in2(not_1_out), .in3(in_2), .in4(in_2), .in5(in_2), .in6(in_2), .in7(in_2),
    .out(multiplexer_1_out), .sel(ABC));  // open: en
  Multiplexer #(.select(3)) multiplexer_2 (
    .in1(D), .in2(in_3), .in3(D), .in4(in_2), .in5(in_2), .in6(in_2), .in7(in_2), .out(multiplexer_2_out),
    .sel(ABC));  // open: in0, en
  Multiplexer #(.select(3)) multiplexer_3 (
    .in0(D), .in1(in_2), .in2(in_3), .in3(D), .in4(in_2), .in5(in_2), .in6(in_2), .in7(in_2),
    .out(multiplexer_3_out), .sel(ABC));  // open: en
  Multiplexer #(.select(3)) multiplexer_4 (
    .in0(in_3), .in1(in_3), .in2(not_1_out), .in3(in_2), .in4(in_2), .in5(in_2), .in6(in_2), .in7(in_2),
    .out(multiplexer_4_out), .sel(ABC));  // open: en
  Multiplexer #(.select(3)) multiplexer_5 (
    .in0(not_1_out), .in1(in_3), .in2(in_2), .in3(in_2), .in4(in_2), .in5(in_2), .in6(in_2), .in7(in_2),
    .out(multiplexer_5_out), .sel(ABC));  // open: en
  Multiplexer #(.select(3)) multiplexer_6 (
    .in0(in_3), .in1(not_1_out), .in2(in_2), .in3(in_2), .in4(in_2), .in5(in_2), .in6(in_2), .in7(in_2),
    .out(multiplexer_6_out), .sel(ABC));  // open: en
  Multiplexer #(.select(3)) multiplexer_7 (
    .in0(D), .in1(in_3), .in2(not_1_out), .in3(not_1_out), .in4(in_2), .in5(in_2), .in6(in_2), .in7(in_2),
    .out(multiplexer_7_out), .sel(ABC));  // open: en
  _7_Segment_Display u_7_segment_display_1 (
    .g(multiplexer_7_out), .f(multiplexer_6_out), .a(multiplexer_1_out), .b(multiplexer_2_out),
    .e(multiplexer_5_out), .d(multiplexer_4_out), .c(multiplexer_3_out));  // open: dp
endmodule
